# Fritzing sketch NFCYoklama Şema (saved by Fritzing 0.9.10b)
stripboards: 1

parts:
  T3_Vakfı1 = Generic shrouded header - 32 pins [package=THT]
  DENEYAP_KART1 = DENEYAP OLED EKRAN [package="DIP (Dual Inline) [THT]"]  # not connected
  Parça1 = RFID-RC522-v3
  R1 = Resistor [tolerance=±5% power=0.25 resistance=10k package=THT]
  JP2 = Header 8 [package=1x08_smd_alt]
  Keypad4x1 = Keypad Membran 4x4
  JP3 = Header 8 [package=1x08_smd_alt]
  JP4 = Header 8 [package=1x08_smd_alt]
  JP5 = Header 8 [package=1x08_smd_alt]
  JP6 = Header 8 [package=1x08_smd_alt]
  SG1 = Buzzer 12mm [part_number=COM-07950 package=buzzer-12mm-ns]

nets:
  N1: T3_Vakfı1.pin1, T3_Vakfı1.pin3, T3_Vakfı1.pin6, T3_Vakfı1.pin9, T3_Vakfı1.pin24, T3_Vakfı1.pin27, T3_Vakfı1.pin30, T3_Vakfı1.pin32, Parça1.SDA, Parça1.MOSI, Parça1.GND, R1.Pin_0, R1.Pin_1, JP2.3, JP2.6, JP2.8, Keypad4x1.Pin5, Keypad4x1.Pin8, JP3.8, JP4.3, JP4.6, JP4.8, JP5.8, JP6.3, JP6.6, JP6.8, SG1.2
  N2: T3_Vakfı1.pin2, T3_Vakfı1.pin7, T3_Vakfı1.pin26, T3_Vakfı1.pin31, Parça1.SCK, Parça1.RST, JP2.2, JP2.7, Keypad4x1.Pin7, JP4.2, JP4.7, JP6.2, JP6.7
  N3: T3_Vakfı1.pin4, T3_Vakfı1.pin8, T3_Vakfı1.pin10, T3_Vakfı1.pin14, T3_Vakfı1.pin19, T3_Vakfı1.pin23, T3_Vakfı1.pin25, T3_Vakfı1.pin29, Parça1.MISO, Parça1.3.3V, JP2.1, JP2.5, Keypad4x1.Pin4, Keypad4x1.Pin6, JP3.3, JP3.7, JP4.1, JP4.5, JP5.3, JP5.7, JP6.1, JP6.5, SG1.1
  N4: T3_Vakfı1.pin5, T3_Vakfı1.pin28, Parça1.IRQ, JP2.4, JP4.4, JP6.4
  N5: T3_Vakfı1.pin11, T3_Vakfı1.pin22, Keypad4x1.Pin3, JP3.6, JP5.6
  N6: T3_Vakfı1.pin12, T3_Vakfı1.pin21, Keypad4x1.Pin2, JP3.5, JP5.5
  N7: T3_Vakfı1.pin13, T3_Vakfı1.pin20, Keypad4x1.Pin1, JP3.4, JP5.4
  N8: T3_Vakfı1.pin15, T3_Vakfı1.pin18, JP3.2, JP5.2
  N9: T3_Vakfı1.pin16, T3_Vakfı1.pin17, JP3.1, JP5.1

custom parts:
  Generic shrouded header - 32 pins: Ülkemizin mühendislik kaynakları kullanılarak geliştirilen Deneyap Kart; güçlü işlemcisi, dayanıklı tasarımı ve çok yönlü giriş/çıkış pinleri ile kullanıcılara Elektronik Programlama, Nesnelerin İnterneti (IoT) ve Yapay Zeka alanlarında başlangıç seviyesinden endüstriyel uygulamalara kadar her seviyede projeyi yapma imkanı sunuyor.
  DENEYAP OLED EKRAN: https://deneyapkart.org/
  RFID-RC522-v3: A simple China made RFID-RC522 Reader (6x4 cm); do check the pin labels, as this is a MFRC522 based clone.
  Keypad Membran 4x4: Membrane Keypad 4x4 Matrix
  Buzzer 12mm: Buzzer 12mm Spark Fun Electronics SKU : Comp-Buzzer Through hole This is a small 12mm round speaker that operates around the audible 2kHz range. You can use these speakers to create simple music or user interfaces. This is not a true piezoelectric speaker but behaves similarly. Instead of a piezoelectric crystal that vibrates with an electric current, this tiny speaker uses an electromagnet to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
